// Digital circuit ELTN32-Digital-Lock.dig as structural Verilog
module ELTN32_Digital_Lock (
);

  wire BadState, BAND, EnterBtn, GAND, IsLocked, IsMatch, not_1_out, not_2_out, not_3_out, or_1_out,
       ResetBtn, UnlockState;
  wire [3:0] CountVal;
  wire [7:0] EntryBus, SecretBus;

  DipSwitch #(.Bits(8)) ENTRY_CODE (.out(EntryBus[0]));
  DipSwitch ENTRY_CODE_2 (.out(EntryBus[1]));
  DipSwitch ENTRY_CODE_3 (.out(EntryBus[2]));
  DipSwitch ENTRY_CODE_4 (.out(EntryBus[3]));
  DipSwitch ENTRY_CODE_5 (.out(EntryBus[4]));
  DipSwitch ENTRY_CODE_6 (.out(EntryBus[5]));
  DipSwitch ENTRY_CODE_7 (.out(EntryBus[6]));
  DipSwitch ENTRY_CODE_8 (.out(EntryBus[7]));
  DipSwitch #(.Bits(8)) SECRET_CODE (.out(SecretBus[0]));
  DipSwitch SECRET_CODE_2 (.out(SecretBus[1]));
  DipSwitch SECRET_CODE_3 (.out(SecretBus[2]));
  DipSwitch SECRET_CODE_4 (.out(SecretBus[3]));
  DipSwitch SECRET_CODE_5 (.out(SecretBus[4]));
  DipSwitch SECRET_CODE_6 (.out(SecretBus[5]));
  DipSwitch SECRET_CODE_7 (.out(SecretBus[6]));
  DipSwitch SECRET_CODE_8 (.out(SecretBus[7]));
  or or_1 (or_1_out, BAND, ResetBtn);
  Counter #(.Bits(4)) counter_1 (.en(1'b1), .C(or_1_out), .clr(ResetBtn), .out(CountVal));  // open: ovf
  Seven_Seg_Hex seven_seg_hex_1 (.d(CountVal), .dp(1'b1));
  Comparator #(.Bits(8)) IsMatchComparator (.a(EntryBus), .b(SecretBus), .eq(IsMatch));  // open: gt, lt
  Comparator #(.Bits(4)) IsLockedComparator (.a(CountVal), .b(4'b0101), .eq(IsLocked));  // open: gt, lt
  not not_1 (not_1_out, IsMatch);
  LED UNLOCKED (.in(GAND));
  LED BAD_CODE (.in(BAND));
  LED LOCKED_OUT (.in(IsLocked));
  not not_2 (not_2_out, IsLocked);
  not not_3 (not_3_out, IsLocked);
  and and_1 (BAND, EnterBtn, not_1_out, not_2_out);
  and and_2 (GAND, EnterBtn, IsMatch, not_3_out);
  RS_FF GoodLatch (.S(GAND), .C(1'b1), .R(ResetBtn), .Q(UnlockState));  // open: nQ
  RS_FF BadLatch (.S(BAND), .C(1'b1), .R(ResetBtn), .Q(BadState));  // open: nQ
  Button ENTER (.out(EnterBtn));
  Button RESET (.out(ResetBtn));
endmodule
